# Fritzing sketch schema (saved by Fritzing 0.9.3b)

parts:
  U1 = ESP32-38PinWide [part_number=ESP32-38PinWide]
  S1 = KY-026
  LED1 = RGB LED (com. cathode, rgb) [package="5 mm [THT]"]

nets:
  N1: U1.3.3, S1.pin3
  N2: U1.GPIO12, S1.pin4
  N3: U1.GND, S1.pin2, LED1.common_cathode
  N4: U1.GPIO2, LED1.red_anode
  N5: U1.GPIO4, LED1.green_anode
  N6: U1.GPIO5, LED1.blue_anode

custom parts:
  ESP32-38PinWide: Generic 38-Pin ESP32 with wide format (only access to one side of pins on a breadboard) based on Stephen Lilley's HiLetgo ESP-WROOM-32 ESP32 ESP-32S Development Board.
  KY-026: ky-026 flame sensor module
